# Fritzing sketch Day-03 (saved by Fritzing 0.9.10b)
breadboards: 1

parts:
  Part1 = Inventr HERO
  R2 = Resistor [tolerance=±5% power=0.25 resistance=220 package=THT]  # not connected
  LED2 = LED - 5mm [color="Red (633nm)" current=0.030 package="5 mm [THT]"]
  S1 = DIP Switch 3 Position
  R3 = Resistor [tolerance=±5% power=0.25 resistance=220 package=THT]

nets:
  N1: Part1.GND, LED2.cathode, R3.Pin_0
  N2: Part1.D2, S1.1, R3.Pin_1
  N3: Part1.5V, S1.6

custom parts:
  Inventr HERO: The inventr hero is a microcontroller board based on the ATmega328 (datasheet). It has 14 digital input/output pins (of which 6 can be used as PWM outputs), 6 analog inputs, a 16 MHz ceramic resonator, a USB connection, a power jack, an ICSP header, and a reset button. It contains everything needed to support the microcontroller; simply connect it to a computer with a USB cable or power it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
