# Fritzing sketch Day-14 (saved by Fritzing 0.9.10b)
breadboards: 1

parts:
  Generic_4x4_button_keypad1 = Generic 4x4 Keypad
  Part2 = Passive Buzzer
  Part3 = Inventr HERO
  LED1 = RGB LED - (4 legs) [package="5 mm [THT]"]
  R4 = Resistor [tolerance=±5% power=0.25 resistance=220 package=THT]
  R5 = Resistor [tolerance=±5% power=0.25 resistance=220 package=THT]
  R6 = Resistor [tolerance=±5% power=0.25 resistance=220 package=THT]

nets:
  N1: Generic_4x4_button_keypad1.C4, Part3.D13/SCK
  N2: Generic_4x4_button_keypad1.C3, Part3.D8
  N3: Generic_4x4_button_keypad1.C2, Part3.D7
  N4: Generic_4x4_button_keypad1.C1, Part3.D6_PWM
  N5: Generic_4x4_button_keypad1.R1, Part3.D5_PWM
  N6: Generic_4x4_button_keypad1.R2, Part3.D4
  N7: Generic_4x4_button_keypad1.R3, Part3.D3_PWM
  N8: Generic_4x4_button_keypad1.R4, Part3.D2
  GND: Part2.GND, Part3.GND, LED1.common_anode
  N9: Part2.S, Part3.D12/MISO
  N10: Part3.D9_PWM, R5.Pin_0
  N11: Part3.D10_PWM/SS, R6.Pin_0
  N12: Part3.D11_PWM/MOSI, R4.Pin_0
  N13: LED1.red_cathode, R4.Pin_1
  N14: LED1.green_cathode, R6.Pin_1
  N15: LED1.blue_cathode, R5.Pin_1

custom parts:
  Generic 4x4 Keypad: generic 4x4 keypad 4 rows of four 6 mm tact switches cheap and nasty but works
  Inventr HERO: The inventr hero is a microcontroller board based on the ATmega328 (datasheet). It has 14 digital input/output pins (of which 6 can be used as PWM outputs), 6 analog inputs, a 16 MHz ceramic resonator, a USB connection, a power jack, an ICSP header, and a reset button. It contains everything needed to support the microcontroller; simply connect it to a computer with a USB cable or power it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
