# Fritzing sketch Day-19 (saved by Fritzing 0.9.10b)

parts:
  Part1 = Arduino Uno (Inventr.io)
  Grove1 = Grove 4 Digit Display
  RE1 = KY-040 Rotary encoder [package=THT]
  Part2 = Passive Buzzer

nets:
  N1: Part1.D10_PWM/SS, Part2.S
  GND: Part1.GND, Grove1.GND, RE1.GND, Part2.GND
  N2: Part1.D2, RE1.CLK
  N3: Part1.D3_PWM, RE1.DT
  N4: Part1.D5_PWM, Grove1.DIO
  N5: Part1.D6_PWM, Grove1.CLK
  N6: Part1.5V#84, RE1.Vcc
  N7: Part1.5V#87, Grove1.VCC

custom parts:
  Arduino Uno (Inventr.io): The Arduino Uno is a microcontroller board based on the ATmega328 (datasheet). It has 14 digital input/output pins (of which 6 can be used as PWM outputs), 6 analog inputs, a 16 MHz ceramic resonator, a USB connection, a power jack, an ICSP header, and a reset button. It contains everything needed to support the microcontroller; simply connect it to a computer with a USB cable or power it with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
  KY-040 Rotary encoder: KY-040 Rotary Encoder with switch on breakout borad from AZ Delivery
