# Fritzing sketch Day-24 (saved by Fritzing 0.9.10b)
breadboards: 1

parts:
  OLED_I2C1 = OLED 128x64 I2C Monochrome Display
  Part2 = Inventr HERO
  inventr1 = Inventr.io 4 Digit 7 Segment Display [part_number=HW-069]
  Mod1 = Passive Buzzer
  S1 = DIP Switch 3 Position
  R5 = Resistor [tolerance=±5% power=0.25 resistance=10k package=THT]
  R6 = Resistor [tolerance=±5% power=0.25 resistance=10k package=THT]
  R7 = Resistor [tolerance=±5% power=0.25 resistance=10k package=THT]

nets:
  N1: OLED_I2C1.SDA, Part2.A4/SDA
  N2: OLED_I2C1.SCK, Part2.A5/SCL
  VDD: OLED_I2C1.VDD, Part2.5V, inventr1.VCC, S1.4, S1.5, S1.6
  GND: OLED_I2C1.GND, Part2.GND, inventr1.GND, Mod1.-, R5.Pin_1, R6.Pin_1, R7.Pin_1
  N3: Part2.D8, S1.2, R6.Pin_0
  N4: Part2.D9_PWM, S1.1, R5.Pin_0
  N5: Part2.D4, inventr1.DIO
  N6: Part2.D5_PWM, inventr1.CLK
  N7: Part2.D6_PWM, Mod1.S
  N8: Part2.D7, S1.3, R7.Pin_0

custom parts:
  Inventr HERO: The inventr hero is a microcontroller board based on the ATmega328 (datasheet). It has 14 digital input/output pins (of which 6 can be used as PWM outputs), 6 analog inputs, a 16 MHz ceramic resonator, a USB connection, a power jack, an ICSP header, and a reset button. It contains everything needed to support the microcontroller; simply connect it to a computer with a USB cable or power it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
  Inventr.io 4 Digit 7 Segment Display: Inventr.io 4 digit 7 segment display fritzing file for the 30 Days Lost in Space Course
